# Fritzing sketch XY-V17B_arduino_uno (saved by Fritzing 0.9.3b)
breadboards: 1

parts:
  R4 = Resistor [tolerance=±5% resistance=1k package=THT]
  R6 = Resistor [tolerance=±5% resistance=2.2k package=THT]
  R3 = Resistor [tolerance=±5% resistance=10k package=THT]
  R2 = Resistor [tolerance=±5% resistance=10k package=THT]
  IC1 = XY-V17B MP3 module [package=V17B-mp3-module-pp]
  R5 = Resistor [tolerance=±5% resistance=1k package=THT]
  R1 = Resistor [tolerance=±5% resistance=10k package=THT]
  SP1 = SPEAKER [package=pcb_mount_speaker]
  SP2 = SPEAKER [package=pcb_mount_speaker]
  MCU = Arduino Uno (Rev3)

nets:
  N1: R4.Pin_0, MCU.D2
  N2: R4.Pin_1, IC1.IO0/TX
  GND: R6.Pin_0, R3.Pin_0, R2.Pin_0, IC1.GND, SP1.+, SP2.+, MCU.GND
  N3: R6.Pin_1, R5.Pin_0, MCU.D3_PWM
  N4: R3.Pin_1, IC1.CON1
  N5: R2.Pin_1, IC1.CON2
  N6: IC1.IO1/RX, IC1.IO2, IC1.IO4, IC1.IO6, R5.Pin_1
  N7: IC1.CON3/BUSY, R1.Pin_1
  VDD: IC1.VDD, MCU.5V
  N8: IC1.3.3V, R1.Pin_0
  N9: IC1.DACL, SP2.-
  N10: IC1.DACR, SP1.-
